# Fritzing sketch Schematic (saved by Fritzing 0.8.3b)
circuit board: 16.9333cm x 5.64444cm
breadboards: 1

parts:
  16_x_2_generic_LCD = LCD screen
  U1 = atmega328 [package=dip]
  SD_card_breakout = mystery part, 6 pins [chip_label=?]
  R1 = Trimmer Potentiometer [maximum_resistance=10kΩ package=THT]
  6V = 4xAA Switchable Battery Pack w/JST connector
  XTAL1 = CRYSTAL - kHz [frequency="16 MHz"]
  C1 = Electrolytic Capacitor [capacitance=47µF voltage=16V package="100 mil [THT, electrolytic]"]
  C2 = Ceramic Capacitor [capacitance=0.1µF package="100 mil [THT, multilayer]"]
  5V_regulator = Voltage Regulator - 5V [package="TO220 [THT]"]
  C3 = Electrolytic Capacitor [capacitance=47µF voltage=16V package="100 mil [THT, electrolytic]"]
  C4 = Ceramic Capacitor [capacitance=0.1µF package="100 mil [THT, multilayer]"]
  C5 = Ceramic Capacitor [capacitance=22pF package="100 mil [THT, multilayer]"]
  C6 = Ceramic Capacitor [capacitance=22pF package="100 mil [THT, multilayer]"]
  R2 = Resistor [tolerance=±5% resistance=10k package=THT]
  S1_ON_/_OFF = Square Pushbutton
  R3 = Resistor [tolerance=±5% resistance=100 package=THT]
  S2 = Pushbutton [package="[THT]"]
  S3 = Pushbutton [package="[THT]"]
  S4 = Pushbutton [package="[THT]"]
  S5 = Pushbutton [package="[THT]"]

nets (from the schematic view):
  GND: 16_x_2_generic_LCD.VSS, 16_x_2_generic_LCD.R/W, 16_x_2_generic_LCD.LED-, U1.GND, SD_card_breakout.pin1, R1.leg2, 6V.NEG, C1.-, C2.0, 5V_regulator.GND, C3.-, C4.0, C5.0, C6.0, S2.Pin_1, S2.Pin_2, S3.Pin_1, S3.Pin_2, S4.Pin_1, S4.Pin_2, S5.Pin_1, S5.Pin_2
  VDD: 16_x_2_generic_LCD.VDD, U1.VCC, SD_card_breakout.pin2, 5V_regulator.output_voltage, C3.+, C4.1, R2.Pin_1
  N1: 16_x_2_generic_LCD.V0, R1.wiper
  N2: 16_x_2_generic_LCD.RS, U1.D9_(PWM)
  N3: 16_x_2_generic_LCD.E, U1.D7
  N4: 16_x_2_generic_LCD.DB4, U1.D5_(PWM)
  N5: 16_x_2_generic_LCD.DB5, U1.D4
  N6: 16_x_2_generic_LCD.DB6, U1.D3_(PWM)
  N7: 16_x_2_generic_LCD.DB7, U1.D2
  N8: 16_x_2_generic_LCD.LED+, R3.Pin_0
  N9: U1.RESET, R2.Pin_0
  N10: U1.XLAT1, XTAL1.pin_0, C6.1
  N11: U1.XLAT2, XTAL1.pin_1, C5.1
  N12: U1.D8, SD_card_breakout.pin3
  N13: U1.D10_(PWM), R3.Pin_1
  N14: U1.D11_(PWM), SD_card_breakout.pin4
  N15: U1.D12, SD_card_breakout.pin6
  N16: U1.D13, SD_card_breakout.pin5
  N17: U1.AVCC, U1.AREF
  N18: U1.A2, S5.Pin_3, S5.Pin_4
  N19: U1.A3, S4.Pin_3, S4.Pin_4
  N20: U1.A4, S3.Pin_3, S3.Pin_4
  N21: U1.A5, S2.Pin_3, S2.Pin_4
  N22: 6V.POS, S1_ON_/_OFF.leg0
  N23: C1.+, C2.1, 5V_regulator.input_voltage, S1_ON_/_OFF.leg1

notes:
  Pushbutons, Atmega328 internal pullup enabled
  BoxOfWords schematic
  Ando Roots <ando@sqroot.eu> 2014
  https://github.com/anroots/box-of-words

custom parts:
  4xAA Switchable Battery Pack w/JST connector: 4xAA Switchable Battery Pack with JST connector
