# Fritzing sketch pcb_fab (saved by Fritzing 0.8.3b)
circuit board: 9.5673cm x 6.09599cm
breadboards: 1

parts:
  U1 = atmega328 [package=dip]
  XTAL1 = Crystal [frequency="16 Mhz" package=THT]
  C1_XTAL = Ceramic Capacitor [capacitance=22pF package="100 mil [THT, multilayer]"]
  C2_XTAL = Ceramic Capacitor [capacitance=22pF package="100 mil [THT, multilayer]"]
  PWR_IN = male pin header, 2 pins [form="♂ (male)"]
  VCC_REG = Voltage Regulator - 5V [package="TO220 [THT]"]
  C3_6V = Ceramic Capacitor [capacitance=0.1µF package="100 mil [THT, multilayer]"]
  C4_6V = Electrolytic Capacitor [capacitance=47µF package="100 mil [THT, electrolytic]"]
  C5_5V = Ceramic Capacitor [capacitance=0.1µF package="100 mil [THT, multilayer]"]
  C6_5V = Electrolytic Capacitor [capacitance=47µF package="100 mil [THT, electrolytic]"]
  BTN_Conn = male pin header, 5 pins [form="♂ (male)"]
  R1_RST = Resistor [tolerance=±5% resistance=10k package=THT]
  SD_Conn = male pin header, 8 pins [form="♂ (male)"]
  AVR_ISP = double row male pin header, 6 pins [form="♂ (male)"]
  J1 = male pin header, 16 pins [form="♂ (male)"]
  R1 = Trimmer Potentiometer [maximum_resistance=10kΩ package=THT]
  R2 = Resistor [tolerance=±5% resistance=100 package=THT]

nets:
  N1: U1.RESET, R1_RST.Pin_0, AVR_ISP.pin5
  N2: U1.D2, J1.pin14
  N3: U1.D3_(PWM), J1.pin13
  N4: U1.D4, J1.pin12
  N5: U1.VCC, U1.AVCC, U1.AREF, VCC_REG.output_voltage, C5_5V.1, C6_5V.+, R1_RST.Pin_1, SD_Conn.pin3, AVR_ISP.pin2, J1.pin2
  GND: U1.GND, C1_XTAL.1, C2_XTAL.1, PWR_IN.pin2, VCC_REG.GND, C3_6V.0, C4_6V.-, C5_5V.0, C6_5V.-, BTN_Conn.pin5, SD_Conn.pin1, SD_Conn.pin8, AVR_ISP.pin6, J1.pin1, J1.pin5, J1.pin16, R1.leg2
  N6: U1.XLAT1, XTAL1.pin_0, C2_XTAL.0
  N7: U1.XLAT2, XTAL1.pin_1, C1_XTAL.0
  N8: U1.D5_(PWM), J1.pin11
  N9: U1.D7, J1.pin6
  N10: U1.D9_(PWM), SD_Conn.pin4, J1.pin4
  N11: U1.D10_(PWM), R2.Pin_0
  N12: U1.D11_(PWM), SD_Conn.pin5, AVR_ISP.pin4
  N13: U1.D12, SD_Conn.pin7, AVR_ISP.pin1
  N14: U1.D13, SD_Conn.pin6, AVR_ISP.pin3
  N15: U1.A2, BTN_Conn.pin4
  N16: U1.A3, BTN_Conn.pin3
  N17: U1.A4, BTN_Conn.pin2
  N18: U1.A5, BTN_Conn.pin1
  N19: PWR_IN.pin1, VCC_REG.input_voltage, C3_6V.1, C4_6V.+
  N20: J1.pin3, R1.wiper
  N21: J1.pin15, R2.Pin_1
